// Logisim project CPU.circ as structural Verilog: 1 circuit, main circuit main
module main (
);

  wire main_1_p2, main_1_p3, main_1_p4;
  wire [4:0] multiplexer_1_out, PC_q, undriven;
  wire [31:0] main_2_rs_output, main_2_rt_output, multiplexer_2_out, ram_1_data;

  Register #(.width(5)) PC (.D(undriven), .Q(PC_q));  // open: en, clk, clr
  RAM #(.addrWidth(5), .dataWidth(32), .bus("asynch")) ram_1 (.addr(PC_q), .data(ram_1_data));  // open: sel, ld, clr
  // Control_Unit_main main_1: pin names not known; wires that end beside it: ram_1_data[31:26], main_1_p2, main_1_p3, main_1_p4
  Multiplexer #(.width(5), .enable("false")) multiplexer_1 (
    .in0(ram_1_data[20:16]), .in1(ram_1_data[15:11]), .out(multiplexer_1_out), .sel(main_1_p2));
  Register_File_main main_2 (
    .Rs_Output(main_2_rs_output), .Rt_Output(main_2_rt_output), .Rs(ram_1_data[25:21]),
    .Rt(ram_1_data[20:16]), .Reg_Write(main_1_p4), .Rd(multiplexer_1_out));  // open: Clock, Write_Data
  Multiplexer #(.width(32), .enable("false")) multiplexer_2 (
    .in0(main_2_rt_output), .out(multiplexer_2_out), .sel(main_1_p3));  // open: in1
  ALU_main main_3 (.Input_one(main_2_rs_output), .Input_two(multiplexer_2_out));  // open: ALu_Op, out_4
endmodule
